// Logisim project scheme.circ as structural Verilog: 17 circuits, main circuit main
module main (
);

  wire and_1_out, cdm_16_1_p2, cdm_16_1_p3, cdm_16_1_p5, cdm_16_1_p6, cdm_16_1_p7, cdm_16_1_p9, cdm_16_1_p10,
       cdm_16_1_p16, clk, controller32white_1_p29, controller32white_1_p30, debugger_1_p1, debugger_1_p2, in,
       in_ctrl_1_p1, in_ctrl_1_p2, in_ctrl_1_p9, mem, not_1_out, or_1_out, pc_move, player_move, ram_1_p4,
       ram_1_p6, ram_1_p9, ram_1_p10, ram_1_p15, ram_1_p18, ram_1_p20, randctrl2_1_p5, randctrl2_1_p12,
       randctrl2_1_p16, randctrl2_1_p21, randctrl2_1_p23, randctrl2_1_p24, randctrl2_1_p25, randctrl2_1_p26,
       read, word;
  wire [6:0] randctrl2_1_p19;
  wire [15:0] addr_bus, bit_extender_1_out, cdm_16_1_p8, controller32white_1_p35, controller32white_1_p36,
       data_bus, in_ctrl_1_p3;
  wire [31:0] controller32black_1_out_5, controller32black_1_out_6, controller32black_1_out_7,
       controller32black_1_out_8, controller32black_1_out_9, controller32black_1_out_10,
       controller32black_1_out_11, controller32black_1_out_12, controller32black_1_out_13,
       controller32black_1_out_14, controller32black_1_out_15, controller32black_1_out_16,
       controller32black_1_out_17, controller32black_1_out_18, controller32black_1_out_19,
       controller32black_1_out_20, controller32black_1_out_21, controller32black_1_out_22,
       controller32black_1_out_23, controller32black_1_out_24, controller32black_1_out_25,
       controller32black_1_out_26, controller32black_1_out_27, controller32black_1_out_28,
       controller32black_1_out_29, controller32white_1_p2, controller32white_1_p5, controller32white_1_p6,
       controller32white_1_p7, controller32white_1_p8, controller32white_1_p9, controller32white_1_p10,
       controller32white_1_p11, controller32white_1_p12, controller32white_1_p13, controller32white_1_p14,
       controller32white_1_p15, controller32white_1_p16, controller32white_1_p17, controller32white_1_p18,
       controller32white_1_p19, controller32white_1_p20, controller32white_1_p21, controller32white_1_p22,
       controller32white_1_p23, controller32white_1_p24, controller32white_1_p25, controller32white_1_p26,
       controller32white_1_p27, controller32white_1_p28;
  wire [31:20] undriven, undriven_2;

  Clock clock_1 (.out(clk));
  // Probe on cdm_16_1_p2
  // CdM_16 cdm_16_1: pin names not known; wires that end beside it: clk, cdm_16_1_p2, cdm_16_1_p3, clk, cdm_16_1_p5, cdm_16_1_p6, cdm_16_1_p7, cdm_16_1_p8, cdm_16_1_p9, cdm_16_1_p10, mem, cdm_16_1_p5, read, cdm_16_1_p6, cdm_16_1_p7, cdm_16_1_p16
  // Debugger debugger_1: pin names not known; wires that end beside it: debugger_1_p1, debugger_1_p2, player_move, cdm_16_1_p9, data_bus
  // Probe on cdm_16_1_p3
  // Probe on addr_bus
  assign data_bus = not_1_out ? cdm_16_1_p8 : 16'bz;  // Controlled_Buffer controlled_buffer_1
  not not_1 (not_1_out, cdm_16_1_p16);
  DotMatrix #(.matrixcols(25), .matrixrows(20)) dotmatrix_1 (
    .col0({20{1'b0}}), .col1(20'h1ffe), .col2({20{1'b0}}), .col3(20'h1ffe), .col4({20{1'b0}}),
    .col5(20'h1ffe), .col6({20{1'b0}}), .col7(20'h1ffe), .col8({20{1'b0}}), .col9(20'h1ffe),
    .col10({20{1'b0}}), .col11(20'h1ffe), .col12({20{1'b0}}), .col13(20'h1ffe), .col14({20{1'b0}}),
    .col15(20'h1ffe), .col16({20{1'b0}}), .col17(20'h1ffe), .col18({20{1'b0}}), .col19(20'h1ffe),
    .col20({20{1'b0}}), .col21(20'h1ffe), .col22({20{1'b0}}), .col23(20'h1ffe), .col24({20{1'b0}}));
  DotMatrix #(.matrixcols(25), .matrixrows(32), .dotshape("circle")) dotmatrix_2 (
    .col0(controller32white_1_p2), .col1(controller32white_1_p5), .col2(controller32white_1_p6),
    .col3(controller32white_1_p7), .col4(controller32white_1_p8), .col5(controller32white_1_p9),
    .col6(controller32white_1_p10), .col7(controller32white_1_p11), .col8(controller32white_1_p12),
    .col9(controller32white_1_p13), .col10(controller32white_1_p14), .col11(controller32white_1_p15),
    .col12(controller32white_1_p16), .col13(controller32white_1_p17), .col14(controller32white_1_p18),
    .col15(controller32white_1_p19), .col16(controller32white_1_p20), .col17(controller32white_1_p21),
    .col18(controller32white_1_p22), .col19(controller32white_1_p23), .col20(controller32white_1_p24),
    .col21(controller32white_1_p25), .col22(controller32white_1_p26), .col23(controller32white_1_p27),
    .col24(controller32white_1_p28));
  DotMatrix #(.matrixcols(25), .matrixrows(32), .dotshape("circle")) dotmatrix_3 (
    .col0(controller32black_1_out_5), .col1(controller32black_1_out_18), .col2(controller32black_1_out_6),
    .col3(controller32black_1_out_19), .col4(controller32black_1_out_7), .col5(controller32black_1_out_20),
    .col6(controller32black_1_out_8), .col7(controller32black_1_out_21), .col8(controller32black_1_out_9),
    .col9(controller32black_1_out_22), .col10(controller32black_1_out_10),
    .col11(controller32black_1_out_23), .col12(controller32black_1_out_11),
    .col13(controller32black_1_out_24), .col14(controller32black_1_out_12),
    .col15(controller32black_1_out_25), .col16(controller32black_1_out_13),
    .col17(controller32black_1_out_26), .col18(controller32black_1_out_14),
    .col19(controller32black_1_out_27), .col20(controller32black_1_out_15),
    .col21(controller32black_1_out_28), .col22(controller32black_1_out_16),
    .col23(controller32black_1_out_29), .col24(controller32black_1_out_17));
  DotMatrix #(.matrixcols(25), .matrixrows(32), .dotshape("circle")) dotmatrix_4 (
    .col0({undriven, {20{1'b0}}}), .col1({undriven_2, 20'h7ff80}), .col2({undriven, {20{1'b0}}}),
    .col3({undriven_2, 20'h7ff80}), .col4({undriven, {20{1'b0}}}), .col5({undriven_2, 20'h7ff80}),
    .col6({undriven, {20{1'b0}}}), .col7({undriven_2, 20'h7ff80}), .col8({undriven, {20{1'b0}}}),
    .col9({undriven_2, 20'h7ff80}), .col10({undriven, {20{1'b0}}}), .col11({undriven_2, 20'h7ff80}),
    .col12({undriven, {20{1'b0}}}), .col13({undriven_2, 20'h7ff80}), .col14({undriven, {20{1'b0}}}),
    .col15({undriven_2, 20'h7ff80}), .col16({undriven, {20{1'b0}}}), .col17({undriven_2, 20'h7ff80}),
    .col18({undriven, {20{1'b0}}}), .col19({undriven_2, 20'h7ff80}), .col20({undriven, {20{1'b0}}}),
    .col21({undriven_2, 20'h7ff80}), .col22({undriven, {20{1'b0}}}), .col23({undriven_2, 20'h7ff80}),
    .col24({undriven, {20{1'b0}}}));
  // controller32white controller32white_1: pin names not known; wires that end beside it: pc_move, controller32white_1_p2, clk, debugger_1_p1, controller32white_1_p5, controller32white_1_p6, controller32white_1_p7, controller32white_1_p8, controller32white_1_p9, controller32white_1_p10, controller32white_1_p11, controller32white_1_p12, controller32white_1_p13, controller32white_1_p14, controller32white_1_p15, controller32white_1_p16, controller32white_1_p17, controller32white_1_p18, controller32white_1_p19, controller32white_1_p20, controller32white_1_p21, controller32white_1_p22, controller32white_1_p23, controller32white_1_p24, controller32white_1_p25, controller32white_1_p26, controller32white_1_p27, controller32white_1_p28, controller32white_1_p29, controller32white_1_p30, read, controller32white_1_p29, controller32white_1_p30, read, controller32white_1_p35, controller32white_1_p36
  controller32black controller32black_1 (
    .clk(clk), .write(debugger_1_p2), .column(controller32white_1_p35), .value(controller32white_1_p36),
    .out_5(controller32black_1_out_5), .out_6(controller32black_1_out_6), .out_7(controller32black_1_out_7),
    .out_8(controller32black_1_out_8), .out_9(controller32black_1_out_9),
    .out_10(controller32black_1_out_10), .out_11(controller32black_1_out_11),
    .out_12(controller32black_1_out_12), .out_13(controller32black_1_out_13),
    .out_14(controller32black_1_out_14), .out_15(controller32black_1_out_15),
    .out_16(controller32black_1_out_16), .out_17(controller32black_1_out_17),
    .out_18(controller32black_1_out_18), .out_24(controller32black_1_out_24),
    .out_19(controller32black_1_out_19), .out_25(controller32black_1_out_25),
    .out_20(controller32black_1_out_20), .out_26(controller32black_1_out_26),
    .out_21(controller32black_1_out_21), .out_27(controller32black_1_out_27),
    .out_22(controller32black_1_out_22), .out_28(controller32black_1_out_28),
    .out_23(controller32black_1_out_23), .out_29(controller32black_1_out_29));
  and and_1 (and_1_out, ram_1_p10, ram_1_p15);
  // NOT_Gate not_2 is placed but not wired
  MEM_WRAP mem_wrap_1 (.addr_bus(addr_bus));
  MEM_WRAP mem_wrap_2 (.addr_bus(addr_bus));
  // RAM ram_1: pin names not known; wires that end beside it: read, data_bus, pc_move, ram_1_p4, ram_1_p4, ram_1_p6, ram_1_p6, word, ram_1_p9, ram_1_p10, and_1_out, ram_1_p9, mem, clk, ram_1_p15, read, read, ram_1_p18, ram_1_p18, ram_1_p20, ram_1_p20, data_bus
  Hex_Digit_Display hex_digit_display_1 ();  // open: value, dp
  randctrl1 randctrl1_1 ();
  TTY #(.cols(40)) tty_1 (.data(data_bus[6:0]), .clk(clk), .we(or_1_out));  // open: clr
  Hex_Digit_Display hex_digit_display_2 ();  // open: value, dp
  // randctrl2 randctrl2_1: pin names not known; wires that end beside it: {20{1'b0}}, 20'h1ffe, addr_bus, in, randctrl2_1_p5, data_bus, data_bus, clk, clk, mem, in, randctrl2_1_p12, randctrl2_1_p5, data_bus, read, randctrl2_1_p16, randctrl2_1_p16, pc_move, randctrl2_1_p19, data_bus, randctrl2_1_p21, randctrl2_1_p21, randctrl2_1_p23, randctrl2_1_p24, randctrl2_1_p25, randctrl2_1_p26
  or or_1 (or_1_out, in, randctrl2_1_p12);
  or or_2 (or_1_out, in, randctrl2_1_p12);
  Keyboard #(.trigger("falling")) keyboard_1 (.clk(clk), .re(in), .data(randctrl2_1_p19));  // open: clr, avail
  turn_changer turn_changer_1 (
    .data_bus(addr_bus), .address_bus_2(addr_bus), .address(16'h1), .memory_2(mem), .read(read), .clk(clk),
    .pc(player_move));
  assign bit_extender_1_out = {{9{1'b0}}, randctrl2_1_p19};  // Bit_Extender bit_extender_1
  assign data_bus = in ? bit_extender_1_out : 16'bz;  // Controlled_Buffer controlled_buffer_2
  OUT_CTRL out_ctrl_1 ();
  OUT_CTRL out_ctrl_2 ();
  // IN_CTRL in_ctrl_1: pin names not known; wires that end beside it: in_ctrl_1_p1, in_ctrl_1_p2, in_ctrl_1_p3, mem, read, in_ctrl_1_p1, in_ctrl_1_p2, in, in_ctrl_1_p9
  // Pins of 20 and 32 bits meet at {undriven, {20{1'b0}}}
  // Pins of 20 and 32 bits meet at {undriven_2, 20'h7ff80}
endmodule

module controller32white (
  input  clk,
  input  write,
  input  [15:0] column,
  input  [15:0] value,
  input  clk_2,
  output [31:0] out_6,
  output [31:0] out_7,
  output [31:0] out_8,
  output [31:0] out_9,
  output [31:0] out_10,
  output [31:0] out_11,
  output [31:0] out_12,
  output [31:0] out_13,
  output [31:0] out_14,
  output [31:0] out_15,
  output [31:0] out_16,
  output [31:0] out_17,
  output [31:0] out_18,
  output [31:0] out_19,
  output [31:0] out_20,
  output [31:0] out_21,
  output [31:0] out_22,
  output [31:0] out_23,
  output [31:0] out_24,
  output [31:0] out_25,
  output [31:0] out_26,
  output [31:0] out_27,
  output [31:0] out_28,
  output [31:0] out_29
);

  wire _1_COL, _2_COL, _4_COL, _6_COL, _8_COL, _9_COL, _10_COL, _11_COL, _12_COL, and_1_out, and_3_out,
       and_4_out, and_5_out, and_6_out, and_8_out, and_9_out, and_10_out, and_11_out, and_12_out, and_13_out,
       and_14_out, and_15_out, and_16_out, and_17_out, and_18_out, and_19_out, and_20_out, and_22_out,
       and_23_out, and_24_out, and_25_out, and_27_out, and_28_out, undriven;
  wire [15:0] _5_COL, _7_COL, reg_top, reg_top_8_q, shifter_bot_white_1_out, shifter_bot_white_2_out,
       shifter_bot_white_3_out, shifter_bot_white_4_out, shifter_bot_white_5_out, shifter_bot_white_6_out,
       shifter_bot_white_7_out, shifter_bot_white_8_out, shifter_bot_white_9_out, shifter_bot_white_11_out,
       shifter_bot_white_12_out, shifter_bot_white_13_out, shifter_top_white_1_out_2,
       shifter_top_white_2_out_2, shifter_top_white_3_out_2, shifter_top_white_4_out_2,
       shifter_top_white_5_out_2, shifter_top_white_6_out_2, shifter_top_white_7_out_2,
       shifter_top_white_8_out_2, shifter_top_white_9_out_2, shifter_top_white_10_out_2,
       shifter_top_white_11_out_2, shifter_top_white_12_out_2;
  wire [15:1] _3_COL, reg_bot_8_q;

  shifter_bot_white shifter_bot_white_1 (.in({_3_COL, write}), .out(shifter_bot_white_1_out));
  and and_1 (and_1_out, ~write, _1_COL, write);  // AND_Gate
  and and_2 (and_1_out, ~write, _1_COL, write);  // AND_Gate
  shifter_top_white shifter_top_white_1 (.in(reg_top), .out_2(shifter_top_white_1_out_2));
  and and_3 (and_3_out, _8_COL, _1_COL, _2_COL);
  shifter_bot_white shifter_bot_white_2 (.in({_3_COL, write}), .out(shifter_bot_white_2_out));
  and and_4 (and_4_out, _7_COL[0], _7_COL[0]);  // AND_Gate
  shifter_top_white shifter_top_white_2 (.in({_3_COL, write}), .out_2(shifter_top_white_2_out_2));
  and and_5 (and_5_out, write, _7_COL[0], write);
  Register #(.width(16), .trigger("falling")) reg_bot (
    .D(shifter_bot_white_1_out), .en(and_1_out), .Q(out_19[15:0]), .clk(clk));  // open: clr
  Register #(.width(16), .trigger("falling")) u_reg_top (
    .D(shifter_top_white_1_out_2), .en(and_3_out), .Q(out_19[31:16]));  // open: clk, clr
  Register #(.width(16), .trigger("falling")) reg_bot_2 (
    .D(shifter_bot_white_2_out), .en(and_4_out), .Q(out_25[15:0]), .clk(clk));  // open: clr
  Register #(.width(16), .trigger("falling")) reg_top_2 (
    .D(shifter_top_white_2_out_2), .en(and_5_out), .Q(out_25[31:16]), .clk(clk));  // open: clr
  shifter_bot_white shifter_bot_white_3 (.in({_3_COL, write}), .out(shifter_bot_white_3_out));
  and and_6 (and_6_out, ~_12_COL, _2_COL, write);  // AND_Gate
  and and_7 (and_6_out, ~_12_COL, _2_COL, write);  // AND_Gate
  shifter_top_white shifter_top_white_3 (.in({_3_COL, write}), .out_2(shifter_top_white_3_out_2));
  and and_8 (and_8_out, write, _2_COL, write);
  shifter_bot_white shifter_bot_white_4 (.in({_3_COL, write}), .out(shifter_bot_white_4_out));
  and and_9 (and_9_out, ~write, _8_COL, write);  // AND_Gate
  shifter_top_white shifter_top_white_4 (.in(reg_top), .out_2(shifter_top_white_4_out_2));
  and and_10 (and_10_out, _1_COL, _8_COL, write);
  Register #(.width(16), .trigger("falling")) reg_bot_3 (
    .D(shifter_bot_white_3_out), .en(and_6_out), .Q(out_20[15:0]), .clk(clk));  // open: clr
  Register #(.width(16), .trigger("falling")) reg_top_3 (
    .D(shifter_top_white_3_out_2), .en(and_8_out), .Q(out_20[31:16]), .clk(clk));  // open: clr
  Register #(.width(16), .trigger("falling")) reg_bot_4 (
    .D(shifter_bot_white_4_out), .en(and_9_out), .Q(out_26[15:0]));  // open: clk, clr
  Register #(.width(16), .trigger("falling")) reg_top_4 (
    .D(shifter_top_white_4_out_2), .en(and_10_out), .Q(out_26[31:16]), .clk(clk));  // open: clr
  shifter_bot_white shifter_bot_white_5 (.in(reg_top), .out(shifter_bot_white_5_out));
  and and_11 (and_11_out, ~write, write, write);  // AND_Gate
  shifter_top_white shifter_top_white_5 (.in({_3_COL, write}), .out_2(shifter_top_white_5_out_2));
  and and_12 (and_12_out, _5_COL[0], write, write);
  shifter_bot_white shifter_bot_white_6 (.in({_3_COL, write}), .out(shifter_bot_white_6_out));
  and and_13 (and_13_out, ~_2_COL, _9_COL, write);  // AND_Gate
  shifter_top_white shifter_top_white_6 (.in({_3_COL, write}), .out_2(shifter_top_white_6_out_2));
  and and_14 (and_14_out, _11_COL, _9_COL, write);
  Register #(.width(16), .trigger("falling")) reg_bot_5 (
    .D(shifter_bot_white_5_out), .en(and_11_out), .Q(out_21[15:0]), .clk(clk));  // open: clr
  Register #(.width(16), .trigger("falling")) reg_top_5 (
    .D(shifter_top_white_5_out_2), .en(and_12_out), .Q(out_21[31:16]), .clk(clk));  // open: clr
  Register #(.width(16), .trigger("falling")) reg_bot_6 (
    .D(shifter_bot_white_6_out), .en(and_13_out), .Q(out_27[15:0]), .clk(clk));  // open: clr
  Register #(.width(16), .trigger("falling")) reg_top_6 (
    .D(shifter_top_white_6_out_2), .en(and_14_out), .Q(out_27[31:16]), .clk(clk));  // open: clr
  shifter_bot_white shifter_bot_white_7 (.in(_5_COL), .out(shifter_bot_white_7_out));
  and and_15 (and_15_out, ~write, _4_COL, write);  // AND_Gate
  shifter_top_white shifter_top_white_7 (.in({_3_COL, write}), .out_2(shifter_top_white_7_out_2));
  and and_16 (and_16_out, write, _4_COL, write);
  shifter_bot_white shifter_bot_white_8 (.in(_7_COL), .out(shifter_bot_white_8_out));
  and and_17 (and_17_out, ~write, _10_COL, write);  // AND_Gate
  shifter_top_white shifter_top_white_8 (.in({_3_COL, write}), .out_2(shifter_top_white_8_out_2));
  and and_18 (and_18_out, write, _10_COL, write);
  Register #(.width(16), .trigger("falling")) reg_bot_7 (
    .D(shifter_bot_white_7_out), .en(and_15_out), .Q(out_22[15:0]), .clk(clk));  // open: clr
  Register #(.width(16), .trigger("falling")) reg_top_7 (
    .D(shifter_top_white_7_out_2), .en(and_16_out), .Q(out_22[31:16]), .clk(clk));  // open: clr
  Register #(.width(16), .trigger("falling")) reg_bot_8 (
    .D(shifter_bot_white_8_out), .en(and_17_out), .Q({reg_bot_8_q, clk_2}), .clk(clk));  // open: clr
  Register #(.width(16), .trigger("falling")) reg_top_8 (
    .D(shifter_top_white_8_out_2), .en(and_18_out), .Q(reg_top_8_q), .clk(clk));  // open: clr
  shifter_bot_white shifter_bot_white_9 (.in({_3_COL, write}), .out(shifter_bot_white_9_out));
  shifter_bot_white shifter_bot_white_10 (.in({_3_COL, write}), .out(shifter_bot_white_9_out));
  and and_19 (and_19_out, ~write, _5_COL[0], write);  // AND_Gate
  shifter_top_white shifter_top_white_9 (.in({_3_COL, write}), .out_2(shifter_top_white_9_out_2));
  and and_20 (and_20_out, write, write);  // AND_Gate
  and and_21 (and_20_out, write, write, write);
  shifter_bot_white shifter_bot_white_11 (.in({_3_COL, write}), .out(shifter_bot_white_11_out));
  and and_22 (and_22_out, ~write, _11_COL, write);  // AND_Gate
  shifter_top_white shifter_top_white_10 (.in({_3_COL, write}), .out_2(shifter_top_white_10_out_2));
  and and_23 (and_23_out, _5_COL[0], _11_COL, write);
  Register #(.width(16), .trigger("falling")) reg_bot_9 (
    .D(shifter_bot_white_9_out), .en(and_19_out), .Q(out_23[15:0]), .clk(clk));  // open: clr
  Register #(.width(16)) DATA (
    .D(shifter_top_white_9_out_2), .en(and_20_out), .Q(out_23[31:16]), .clk(clk));  // open: clr
  Register #(.width(16), .trigger("falling")) reg_bot_10 (
    .D(shifter_bot_white_11_out), .en(and_22_out), .Q(out_28[15:0]), .clk(clk));  // open: clr
  Register #(.width(16), .trigger("falling")) reg_top_9 (
    .D(shifter_top_white_10_out_2), .en(and_23_out), .Q(out_28[31:16]), .clk(clk));  // open: clr
  shifter_bot_white shifter_bot_white_12 (.in({_3_COL, write}), .out(shifter_bot_white_12_out));
  Register #(.width(16), .trigger("falling")) reg_bot_11 (
    .D(shifter_bot_white_12_out), .en(and_24_out), .Q(out_24[15:0]), .clk(clk), .clr(undriven));
  Register #(.width(16), .trigger("falling")) reg_bot_12 (
    .D(shifter_bot_white_12_out), .en(and_24_out), .Q(out_24[15:0]), .clk(clk), .clr(undriven));
  and and_24 (and_24_out, ~write, _6_COL, write);  // AND_Gate
  Register #(.width(16), .trigger("falling")) reg_top_10 (
    .D(shifter_top_white_11_out_2), .en(and_25_out), .Q(out_24[31:16]), .clk(clk));  // open: clr
  shifter_top_white shifter_top_white_11 (.in({_3_COL, write}), .out_2(shifter_top_white_11_out_2));
  and and_25 (and_25_out, write, _6_COL, write);
  and and_26 (and_25_out, write, _6_COL, write);
  Register #(.width(16), .trigger("falling")) reg_bot_13 (
    .D(shifter_bot_white_13_out), .en(and_27_out), .Q(out_29[15:0]), .clk(clk));  // open: clr
  shifter_bot_white shifter_bot_white_13 (.in({_3_COL, write}), .out(shifter_bot_white_13_out));
  and and_27 (and_27_out, _12_COL, write);
  shifter_top_white shifter_top_white_12 (.in({_3_COL, write}), .out_2(shifter_top_white_12_out_2));
  Register #(.width(16), .trigger("falling")) reg_top_11 (
    .D(shifter_top_white_12_out_2), .en(and_28_out), .Q(out_29[31:16]), .clk(clk));  // open: clr
  and and_28 (and_28_out, write, _12_COL, write);
  // Pins of 1 and 16 bits meet at _5_COL
  // Pins of 1 and 16 bits meet at {_3_COL, write}
  // Pins of 1 and 16 bits meet at _7_COL
  // Pins of 1 and 32 bits meet at {reg_top_8_q, reg_bot_8_q, clk_2}

  assign out_6 = {32{1'b0}};
  assign out_7 = {32{1'b0}};
  assign out_8 = {32{1'b0}};
  assign out_9 = {32{1'b0}};
  assign out_10 = {32{1'b0}};
  assign out_11 = {32{1'b0}};
  assign out_12 = {32{1'b0}};
  assign out_13 = {32{1'b0}};
  assign out_14 = {32{1'b0}};
  assign out_15 = {32{1'b0}};
  assign out_16 = {32{1'b0}};
  assign out_17 = {32{1'b0}};
  assign out_18 = {32{1'b0}};

  // Other names for the same wires on the sheet: _3_COL[0] = write; column_t[15:0] = {_3_COL, write};
  //   DATA[15:0] = {_3_COL, write}; w[15:0] = {_3_COL, write}

  // Notes on the sheet:
  //   0 - bot, 1 - top
  //   0 - bot, 1 - top
endmodule

module turn_changer (
  input  [15:0] data_bus,
  input  [15:0] address_bus,
  input  [15:0] address_bus_2,
  input  [15:0] address,
  input  memory,
  input  memory_2,
  input  read,
  input  clk,
  output pc
);

  wire and_1_out, and_2_out, comparator_1_eq;
  wire [15:0] address_q;

  Comparator #(.width(16)) comparator_1 (.a(address_bus), .b(address), .eq(comparator_1_eq));  // open: gt, lt
  and and_1 (and_1_out, comparator_1_eq, memory, ~read);  // AND_Gate
  Register #(.width(16), .tristate("false")) u_address (
    .D(data_bus), .en(and_1_out), .Q(address_q), .clk(clk));  // open: clr
  and and_2 (and_2_out, ~address_q[0], ~address_q[7]);  // AND_Gate
  and and_3 (pc, address_q[0], ~address_q[7]);  // AND_Gate

  assign address_bus_2 = address_bus;
  assign memory_2 = memory;
endmodule

module value_converter (
  input  [3:0] value,
  output [15:0] out
);

  ROM #(.addrWidth(4), .dataWidth(16)) rom_1 (.addr(value), .data(out));  // open: sel

  // Notes on the sheet:
  //   contents of rom_1 (hex, n*v repeats v):
  //   0 1 3 7 f 1f 3f 7f ff 1ff 3ff 7ff fff
endmodule

module MEM_WRAP (
  input  [15:0] in_1,
  input  [15:0] data_bus,
  input  [15:0] addr_bus,
  input  clk,
  input  read,
  output [15:0] bus_0,
  output [15:0] bus_0_2,
  output [15:0] out_8
);

  wire and_1_out, and_3_out, comparator_1_lt, comparator_2_eq, undriven, undriven_4, undriven_6, undriven_7,
       undriven_8, undriven_10, undriven_12;
  wire [3:0] undriven_9;
  wire [4:0] undriven_11;
  wire [15:0] bus_1, register_1_q, register_3_q, undriven_2, undriven_3, undriven_5;

  // Probe on in_1
  Subtractor #(.width(16)) subtractor_1 (.a(in_1), .b(16'hff00));  // open: out, bin, bout
  Comparator #(.width(16)) comparator_1 (.a(undriven_2), .lt(comparator_1_lt));  // open: b, gt, eq
  Comparator #(.width(16)) comparator_2 (.a(bus_1), .b(16'hff4a), .eq(comparator_2_eq));  // open: gt, lt
  and and_1 (and_1_out, comparator_2_eq, ~undriven_4);  // AND_Gate
  and and_2 (and_1_out, comparator_2_eq, ~undriven_4);  // AND_Gate
  Shifter #(.width(16), .shift("ar")) shifter_1 (.in(undriven_3), .\dist (4'b0001));  // open: out
  Register #(.width(16), .trigger("falling")) register_1 (
    .D(undriven_5), .en(and_3_out), .Q(register_1_q), .clk(clk), .clr(undriven_6));
  Register #(.width(16), .trigger("falling")) register_2 (
    .D(undriven_5), .en(and_3_out), .Q(register_1_q), .clk(clk), .clr(undriven_6));
  and and_3 (and_3_out, comparator_1_lt, ~undriven);  // AND_Gate
  // Probe on nothing
  // Probe on undriven_10
  Register #(.width(16), .trigger("falling")) register_3 (
    .D(register_3_q), .en(undriven_7), .Q(register_3_q), .clk(clk), .clr(undriven_8));
  Register #(.width(16), .trigger("falling")) register_4 (
    .D(register_3_q), .en(undriven_7), .Q(register_3_q), .clk(clk), .clr(undriven_8));
  value_converter value_converter_1 (.value(undriven_9), .out(bus_0));
  value_converter value_converter_2 (.value(undriven_9), .out(bus_0));
  column_converter column_converter_1 (.in(undriven_11), .out_2(out_8));
  column_converter column_converter_2 (.in(undriven_11), .out_2(out_8));
  // Probe on undriven_12

  assign bus_0_2 = bus_0;

  // Other names for the same wires on the sheet: addr_bus_t[15:0] = in_1
endmodule

module column_converter (
  input  [4:0] in,
  output [15:0] out,
  output [15:0] out_2
);

  ROM #(.addrWidth(5), .dataWidth(16)) rom_1 (.addr(in), .data(out));  // open: sel

  assign out_2 = out;

  // Notes on the sheet:
  //   contents of rom_1 (hex, n*v repeats v):
  //   0 2 4 8 10 20 40 80 100 200 400 800 1000 1001 801 401 201 101 81 41 21 11 9 5 3
endmodule

module inverter (
  input  [15:0] in,
  output [15:0] in_2
);


  assign in_2 = {in[0], in[1], in[2], in[3], in[4], in[5], in[6], in[7], in[8], in[9], in[10], in[11], in[12], in[13], in[14], in[15]};
endmodule

module shifter_top_white (
  input  [15:0] in,
  output [15:0] out,
  output [15:0] out_2
);

  wire [15:0] inverter_1_in_2;

  inverter inverter_1 (.in(in), .in_2(inverter_1_in_2));
  inverter inverter_2 (.in(in), .in_2(inverter_1_in_2));
  inverter inverter_3 (.in(in), .in_2(inverter_1_in_2));
  Shifter #(.width(16), .shift("lr")) shifter_1 (.in(inverter_1_in_2), .\dist (4'b0101), .out(out));
  Shifter #(.width(16), .shift("lr")) shifter_2 (.in(inverter_1_in_2), .\dist (4'b0101), .out(out));

  assign out_2 = out;
endmodule

module shifter_bot_white (
  input  [15:0] in,
  output [15:0] out
);

  wire [3:0] undriven;

  Shifter #(.width(16), .tristate("false")) u_in (.in(in), .\dist (undriven), .out(out));
endmodule

module controller32black (
  input  clk,
  input  write,
  input  [15:0] column,
  input  [15:0] value,
  output [31:0] out_5,
  output [31:0] out_6,
  output [31:0] out_7,
  output [31:0] out_8,
  output [31:0] out_9,
  output [31:0] out_10,
  output [31:0] out_11,
  output [31:0] out_12,
  output [31:0] out_13,
  output [31:0] out_14,
  output [31:0] out_15,
  output [31:0] out_16,
  output [31:0] out_17,
  output [31:0] out_18,
  output [31:0] out_19,
  output [31:0] out_20,
  output [31:0] out_21,
  output [31:0] out_22,
  output [31:0] out_23,
  output [31:0] out_24,
  output [31:0] out_25,
  output [31:0] out_26,
  output [31:0] out_27,
  output [31:0] out_28,
  output [31:0] out_29
);

  wire and_1_out, and_2_out, and_3_out, and_4_out, and_5_out, and_6_out, and_7_out, and_8_out, and_9_out,
       and_10_out, and_11_out, and_12_out, and_14_out, and_15_out, and_16_out, and_18_out, and_19_out,
       and_20_out, and_21_out, and_22_out, and_23_out, and_24_out, and_25_out, shifter_top_black_8_p2,
       undriven;
  wire [15:0] reg_bot_7_q, reg_top, reg_top_7_q, shifter_bot_black_1_out, shifter_bot_black_2_out,
       shifter_bot_black_3_out, shifter_bot_black_4_out, shifter_bot_black_5_out, shifter_bot_black_6_out,
       shifter_bot_black_7_out, shifter_bot_black_8_out, shifter_bot_black_9_out, shifter_bot_black_10_out,
       shifter_bot_black_11_out, shifter_bot_black_12_out, shifter_top_black_1_out, shifter_top_black_2_out,
       shifter_top_black_3_out, shifter_top_black_4_out, shifter_top_black_5_out, shifter_top_black_6_out,
       shifter_top_black_7_out, shifter_top_black_9_out, shifter_top_black_10_out, shifter_top_black_11_out,
       shifter_top_black_12_out;
  wire [31:0] undriven_2;

  shifter_bot_black shifter_bot_black_1 (.out(shifter_bot_black_1_out));
  and and_1 (and_1_out, column[1], column[0]);  // AND_Gate
  shifter_top_black shifter_top_black_1 (.in({value[15:1], column[0]}), .out(shifter_top_black_1_out));
  and and_2 (and_2_out, column[0], column[0]);  // AND_Gate
  shifter_bot_black shifter_bot_black_2 (.out(shifter_bot_black_2_out));
  and and_3 (and_3_out, ~column[11], column[7], column[0]);  // AND_Gate
  shifter_top_black shifter_top_black_2 (.in(reg_top), .out(shifter_top_black_2_out));
  and and_4 (and_4_out, column[0], column[7], column[0]);
  Register #(.width(16)) reg_bot (
    .D(shifter_bot_black_1_out), .en(and_1_out), .Q(out_18[15:0]), .clk(clk));  // open: clr
  Register #(.width(16)) u_reg_top (
    .D(shifter_top_black_1_out), .en(and_2_out), .Q(out_18[31:16]), .clk(clk));  // open: clr
  Register #(.width(16)) reg_bot_2 (
    .D(shifter_bot_black_2_out), .en(and_3_out), .Q(out_24[15:0]), .clk(clk));  // open: clr
  Register #(.width(16)) reg_top_2 (
    .D(shifter_top_black_2_out), .en(and_4_out), .Q(out_24[31:16]), .clk(clk));  // open: clr
  shifter_bot_black shifter_bot_black_3 (.out(shifter_bot_black_3_out));
  and and_5 (and_5_out, ~column[12], column[0], column[0]);  // AND_Gate
  shifter_top_black shifter_top_black_3 (.in({value[15:1], column[0]}), .out(shifter_top_black_3_out));
  and and_6 (and_6_out, column[0], column[2], column[0]);
  shifter_bot_black shifter_bot_black_4 (.out(shifter_bot_black_4_out));
  and and_7 (and_7_out, ~column[0], column[8], column[0]);  // AND_Gate
  shifter_top_black shifter_top_black_4 (.in({value[15:1], column[0]}), .out(shifter_top_black_4_out));
  and and_8 (and_8_out, column[0], column[8], column[5]);
  Register #(.width(16)) reg_bot_3 (
    .D(shifter_bot_black_3_out), .en(and_5_out), .Q(out_19[15:0]), .clk(clk));  // open: clr
  Register #(.width(16)) reg_top_3 (
    .D(shifter_top_black_3_out), .en(and_6_out), .Q(out_19[31:16]), .clk(clk));  // open: clr
  Register #(.width(16)) reg_bot_4 (
    .D(shifter_bot_black_4_out), .en(and_7_out), .Q(out_25[15:0]), .clk(clk));  // open: clr
  Register #(.width(16)) reg_top_4 (
    .D(shifter_top_black_4_out), .en(and_8_out), .Q(out_25[31:16]), .clk(clk));  // open: clr
  shifter_bot_black shifter_bot_black_5 (.out(shifter_bot_black_5_out));
  and and_9 (and_9_out, ~column[0], column[3], column[0]);  // AND_Gate
  shifter_top_black shifter_top_black_5 (.in({value[15:1], column[0]}), .out(shifter_top_black_5_out));
  and and_10 (and_10_out, column[0], column[3], column[0]);
  shifter_bot_black shifter_bot_black_6 (.out(shifter_bot_black_6_out));
  and and_11 (and_11_out, ~column[0], column[9], column[3]);  // AND_Gate
  shifter_top_black shifter_top_black_6 (.in({value[15:1], column[0]}), .out(shifter_top_black_6_out));
  and and_12 (and_12_out, column[0], column[9], column[0]);
  and and_13 (and_12_out, column[0], column[9], column[0]);
  Register #(.width(16)) reg_bot_5 (
    .D(shifter_bot_black_5_out), .en(and_9_out), .Q(out_20[15:0]), .clk(clk));  // open: clr
  Register #(.width(16)) reg_top_5 (
    .D(shifter_top_black_5_out), .en(and_10_out), .Q(out_20[31:16]), .clk(clk));  // open: clr
  Register #(.width(16)) reg_bot_6 (
    .D(shifter_bot_black_6_out), .en(and_11_out), .Q(out_26[15:0]), .clk(clk));  // open: clr
  Register #(.width(16)) reg_top_6 (
    .D(shifter_top_black_6_out), .en(and_12_out), .Q(out_26[31:16]), .clk(clk));  // open: clr
  shifter_bot_black shifter_bot_black_7 (.out(shifter_bot_black_7_out));
  and and_14 (and_14_out, ~column[0], column[4], column[0]);  // AND_Gate
  shifter_top_black shifter_top_black_7 (.in({value[15:1], column[0]}), .out(shifter_top_black_7_out));
  and and_15 (and_15_out, column[0], undriven, column[0]);
  shifter_bot_black shifter_bot_black_8 (.out(shifter_bot_black_8_out));
  buf and_16 (and_16_out, column[0]);  // AND_Gate
  // shifter_top_black shifter_top_black_8: pin names not known; wires that end beside it: {value[15:1], column[0]}, shifter_top_black_8_p2, clk, out_27[31:16]
  and and_17 (shifter_top_black_8_p2, column[0], column[10], column[0]);
  Register #(.width(16)) reg_bot_7 (
    .D(shifter_bot_black_7_out), .en(and_14_out), .Q(reg_bot_7_q), .clk(clk));  // open: clr
  Register #(.width(16)) reg_top_7 (
    .D(shifter_top_black_7_out), .en(and_15_out), .Q(reg_top_7_q), .clk(clk));  // open: clr
  Register #(.width(16)) reg_bot_8 (
    .D(shifter_bot_black_8_out), .en(and_16_out), .Q(out_27[15:0]), .clk(clk));  // open: clr
  shifter_bot_black shifter_bot_black_9 (.out(shifter_bot_black_9_out));
  and and_18 (and_18_out, ~column[0], column[5], column[0]);  // AND_Gate
  shifter_top_black shifter_top_black_9 (.in({value[15:1], column[0]}), .out(shifter_top_black_9_out));
  and and_19 (and_19_out, column[0], column[5], column[0]);
  shifter_bot_black shifter_bot_black_10 (.out(shifter_bot_black_10_out));
  and and_20 (and_20_out, ~column[0], column[11], column[0]);  // AND_Gate
  shifter_top_black shifter_top_black_10 (.in(reg_top), .out(shifter_top_black_10_out));
  and and_21 (and_21_out, column[0], column[11], column[0]);
  Register #(.width(16)) reg_bot_9 (
    .D(shifter_bot_black_9_out), .en(and_18_out), .Q(out_22[15:0]), .clk(clk));  // open: clr
  Register #(.width(16)) reg_top_8 (
    .D(shifter_top_black_9_out), .en(and_19_out), .Q(out_22[31:16]), .clk(clk));  // open: clr
  Register #(.width(16), .tristate("false")) u_column (
    .D(shifter_bot_black_10_out), .en(and_20_out), .Q(out_28[15:0]), .clk(clk));  // open: clr
  Register #(.width(16)) reg_top_9 (
    .D(shifter_top_black_10_out), .en(and_21_out), .Q(out_28[31:16]), .clk(undriven_2[0]));  // open: clr
  shifter_bot_black shifter_bot_black_11 (.out(shifter_bot_black_11_out));
  Register #(.width(16)) reg_bot_10 (
    .D(shifter_bot_black_11_out), .en(and_22_out), .Q(out_23[15:0]), .clk(clk));  // open: clr
  and and_22 (and_22_out, column[6], column[0]);
  shifter_top_black shifter_top_black_11 (.in({value[15:1], column[0]}), .out(shifter_top_black_11_out));
  Register #(.width(16)) reg_top_10 (
    .D(shifter_top_black_11_out), .en(and_23_out), .Q(out_23[31:16]), .clk(clk));  // open: clr
  and and_23 (and_23_out, column[0], column[6], column[0]);
  shifter_bot_black shifter_bot_black_12 (.out(shifter_bot_black_12_out));
  Register #(.width(16)) reg_bot_11 (
    .D(shifter_bot_black_12_out), .en(and_24_out), .Q(out_29[15:0]), .clk(clk));  // open: clr
  and and_24 (and_24_out, ~column[0], column[12], column[0]);  // AND_Gate
  Register #(.width(16)) reg_top_11 (
    .D(shifter_top_black_12_out), .en(and_25_out), .Q(out_29[31:16]), .clk(clk));  // open: clr
  shifter_top_black shifter_top_black_12 (.in({value[15:1], column[0]}), .out(shifter_top_black_12_out));
  and and_25 (and_25_out, column[0], column[12], column[0]);
  // Pins of 1 and 16 bits meet at {value[15:1], column[0]}
  // Pins of 1 and 32 bits meet at undriven_2

  assign out_5 = {32{1'b0}};
  assign out_6 = {32{1'b0}};
  assign out_7 = {32{1'b0}};
  assign out_8 = {32{1'b0}};
  assign out_9 = {32{1'b0}};
  assign out_10 = {32{1'b0}};
  assign out_11 = {32{1'b0}};
  assign out_12 = {32{1'b0}};
  assign out_13 = {32{1'b0}};
  assign out_14 = {32{1'b0}};
  assign out_15 = {32{1'b0}};
  assign out_16 = {32{1'b0}};
  assign out_17 = {32{1'b0}};
  assign value[0] = column[0];
  assign write = column[0];

  // Other names for the same wires on the sheet: column_t[15:0] = {value[15:1], column[0]};
  //   DATA[15:0] = {value[15:1], column[0]}; w[15:0] = {value[15:1], column[0]}; _1_COL = column[1];
  //   _2_COL = column[2]; _3_COL = column[3]; _4_COL = column[4]; _5_COL = column[5]; _6_COL = column[6];
  //   _7_COL = column[7]; _8_COL = column[8]; _9_COL = column[9]; _10_COL = column[10]; _11_COL = column[11];
  //   _12_COL = column[12]

  // Notes on the sheet:
  //   0 - bot, 1 - top
endmodule

module shifter_top_black (
  input  [15:0] in,
  output [15:0] out
);
endmodule

module shifter_bot_black (
  output [15:0] out
);

  wire [15:0] undriven;

  Shifter #(.width(16)) shifter_1 (.in(undriven), .\dist (4'b0100), .out(out));
  Shifter #(.width(16)) shifter_2 (.in(undriven), .\dist (4'b0100), .out(out));
  Shifter #(.width(16)) shifter_3 (.in(undriven), .\dist (4'b0100), .out(out));
endmodule

module OUT_CTRL (
  input  [15:0] addr_bus,
  input  mem,
  input  read,
  output bus_0
);

  wire comparator_1_eq;

  Comparator #(.width(16)) comparator_1 (.a(16'hdeb0), .b(addr_bus), .eq(comparator_1_eq));  // open: gt, lt
  and and_1 (bus_0, comparator_1_eq, mem, ~read);  // AND_Gate
endmodule

module IN_CTRL (
  input  [15:0] addr_bus,
  input  addr_bus_2,
  input  read,
  input  read_2,
  output bus_0
);

  wire comparator_1_eq, read_t;

  Comparator #(.width(16)) comparator_1 (.a(16'hdeae), .b(addr_bus), .eq(comparator_1_eq));  // open: gt, lt
  and and_1 (bus_0, comparator_1_eq, addr_bus_2, read_t);

  // Other names for the same wires on the sheet: mem = addr_bus_2
endmodule

module randctrl1 (
  input  [15:0] in_1,
  input  [15:0] data_bus,
  input  clk,
  input  mem,
  output [3:0] out
);

  wire and_1_p4, comparator_1_eq, mem_t, read;

  Comparator #(.width(16)) comparator_1 (.b(in_1), .eq(comparator_1_eq));  // open: a, gt, lt
  // AND_Gate and_1: pin names not known; wires that end beside it: read, comparator_1_eq, mem_t, and_1_p4

  // Other names for the same wires on the sheet: addr_bus[15:0] = in_1
endmodule

module matrix_register_white (
  input  [15:0] DATA,
  input  mem,
  input  column,
  input  read,
  input  write
);

  wire and_1_out, undriven, undriven_2;
  wire [15:0] reg_top_q, shifter_top_white_1_out_2;

  shifter_top_white shifter_top_white_1 (.in(DATA), .out_2(shifter_top_white_1_out_2));
  and and_1 (and_1_out, column, undriven, write);
  Register #(.width(16), .trigger("falling")) reg_top (
    .D(shifter_top_white_1_out_2), .en(and_1_out), .Q(reg_top_q), .clk(undriven_2));  // open: clr
endmodule

module matrix_register_black (
  input  [15:0] addr_bus,
  input  [15:0] data_bus,
  input  EQ_in,
  input  A_bit,
  input  read,
  input  B_bit,
  input  clk,
  input  GT_in,
  input  LT_in,
  output [31:0] out_10,
  output GT_out,
  output LT_out,
  output A___B
);

  wire and_5_out, comparator_1_eq, comparator_1_gt, comparator_1_lt, mem;

  // AND_Gate and_1 is placed but not wired
  // AND_Gate and_2 is placed but not wired
  // XNOR_Gate xnor_1 is placed but not wired
  // AND_Gate and_3 is placed but not wired
  Comparator #(.width(16)) comparator_1 (
    .a(16'hff4d), .b(addr_bus), .gt(comparator_1_gt), .eq(comparator_1_eq), .lt(comparator_1_lt));
  Comparator #(.width(16)) comparator_2 (
    .a(16'hff4d), .b(addr_bus), .gt(comparator_1_gt), .eq(comparator_1_eq), .lt(comparator_1_lt));
  // AND_Gate and_4 is placed but not wired
  // OR_Gate or_1 is placed but not wired
  and and_5 (and_5_out, comparator_1_eq, mem, ~read);  // AND_Gate
  and and_6 (and_5_out, comparator_1_eq, mem, ~read);  // AND_Gate
  // _1BitComp 1bitcomp_1: pin names not known; wires that end beside it: GT_out, out_10
  Register #(.width(16)) register_1 (.D(data_bus), .en(and_5_out), .clk(clk));  // open: Q, clr
  // _1BitComp 1bitcomp_2: pin names not known; wires that end beside it: LT_out
  // _1BitComp 1bitcomp_3: pin names not known
  // _1BitComp 1bitcomp_4: pin names not known
endmodule
